# Fritzing sketch ECE385_Lab2A_redoBB_bqr (saved by Fritzing 0.9.4)
breadboards: 3

parts:
  U3 = 74153 Dual 4:1 MUX [part_number=74153 package="DIP16 [THT]"]
  U6 = 7400 4 x 2 Input NAND Gate [part_number=7400 package="DIP (Dual Inline) [THT]"]
  U7 = 7486 4 x 2 Input XOR Gate [part_number=7486 package="DIP (Dual Inline) [THT]"]
  U8 = 7402 4 x 2 Input NOR Gate [part_number=7402 package="DIP (Dual Inline) [THT]"]
  U9 = 74153 Dual 4:1 MUX [part_number=74153 package="DIP16 [THT]"]
  U10 = 74161 4 Bit Synchronous Up Down Counter [part_number=74161 package="DIP16 [THT]"]
  U11 = 7474 Dual Positive Edge Triggered D Flip Flop [part_number=7474 package="DIP (Dual Inline) [THT]"]
  U12 = 7402 4 x 2 Input NOR Gate [part_number=7402 package="DIP (Dual Inline) [THT]"]
  U13 = 74194 4 Bit Bi-Directional Shift Register [part_number=74194 package="DIP16 [THT]"]
  U14 = 74194 4 Bit Bi-Directional Shift Register [part_number=74194 package="DIP16 [THT]"]
  U16 = 7400 4 x 2 Input NAND Gate [part_number=7400 package="DIP (Dual Inline) [THT]"]
  U18 = 7400 4 x 2 Input NAND Gate [part_number=7400 package="DIP (Dual Inline) [THT]"]
  U17 = 7427 3 x 3 Input NOR Gate [part_number=7427 package="DIP (Dual Inline) [THT]"]

nets:
  GND: U3.D0, U3.G1, U3.G0, U3.GND, U3.D1, U6.GND, U7.GND, U8.GND, U9.G1, U9.G0, U9.GND, U10.3, U10.4, U10.5, U10.6, U10.GND, U11.GND, U12.GND, U13.GND, U14.GND, U16.GND, U18.GND, U17.GND
  NOR: U3.C0, U8.Q1
  f_prelim: U3.Y0, U7.B4
  F1: U3.S1
  NAND: U3.A0, U6.Q1
  XNOR: U3.B0, U6.B2
  F0: U3.S0
  5V: U3.VCC, U6.VDD, U7.VDD, U8.VDD, U9.VCC, U10.1, U10.7, U10.10, U10.VCC, U11.Q3, U11.B4, U11.VDD, U12.VDD, U13.1, U13.VCC, U14.1, U14.VCC, U16.VDD, U18.VDD, U17.VDD
  A: U6.A1, U7.A1, U8.A1, U9.A0, U9.B0, U9.D1, U13.15
  B: U6.B1, U7.B1, U8.B1, U9.D0, U9.C1, U9.A1, U14.15
  N1: U6.Q2, U6.A2, U7.Q1
  f(A,B): U6.A3, U9.C0, U9.B1
  N2: U6.B3, U6.Q3, U7.Q4
  F2: U7.A4
  A*/B*: U9.Y1, U9.Y0, U13.2, U14.2
  R1: U9.S1
  R0: U9.S0
  CLK: U10.2, U11.Q4, U13.11, U14.11
  Shift: U10.9
  C1: U10.13, U17.Q2, U17.Q3
  C0: U10.14, U17.Q1, U17.Q4
  Q‘: U11.A3, U16.B4
  N3: U11.A4, U16.Q1
  N4: U12.A1, U18.A1, U18.B1
  LOAD_A: U12.B1, U13.10
  S: U12.Q1, U12.A2, U16.A3
  N5: U12.Q2, U18.Q2, U18.A2
  LOAD_B: U12.B2, U14.10
  D0: U13.3, U14.3
  D1: U13.4, U14.4
  D2: U13.5, U14.5
  D3: U13.6, U14.6
  S0_regA: U13.9, U18.Q1
  S0_regB: U14.9, U18.B2
  N6: U16.A1, U16.B1, U17.A3
  N7: U16.Q2, U16.A2, U16.Q4
  N8: U16.B2, U17.A2
  S': U16.B3, U16.Q3, U17.B2
  E: U16.A4, U17.B3

notes:
  SHIFT REGISTERS
  COMPUTATION
  ROUTING
  CONTROL UNIT

custom parts:
  74153 Dual 4:1 MUX: 74153 Dual 4:1 Multiplexor
  7427 3 x 3 Input NOR Gate: 7427 3 x 2 Input NOR Gate
