# Fritzing sketch lab2 (saved by Fritzing 0.9.4)
breadboards: 2

parts:
  U1 = 74194 4 Bit Bi-Directional Shift Register [part_number=74194 package="DIP16 [THT]"]
  U2 = 74194 4 Bit Bi-Directional Shift Register [part_number=74194 package="DIP16 [THT]"]
  U3 = 74153 Dual 4:1 MUX [part_number=74153 package="DIP16 [THT]"]
  U4 = 74153 Dual 4:1 MUX [part_number=74153 package="DIP16 [THT]"]

nets:
  N1: U1.7, U3.Y0
  GND: U1.GND, U2.GND
  VCC: U1.VCC, U2.VCC
  GND_2: U3.G0, U3.GND, U4.GND
  VCC_2: U3.VCC, U4.VCC

notes:
  D3
  D2
  D1
  D0

custom parts:
  74153 Dual 4:1 MUX: 74153 Dual 4:1 Multiplexor
